# Fritzing sketch PainelNano (saved by Fritzing 0.9.3b)
breadboards: 1

parts:
  Componente1 = Arduino Nano (Rev3.0)
  Squix1 = OLED 0.96" 128x64 I2C SSD1306
  M1 = BME280
  Componente2 = RTC DS3231
  R1 = Resistor [tolerance=±5% resistance=10k package=THT]
  VCC1 = Battery block 9V

nets:
  GND: Componente1.GND, Squix1.GND, M1.GND, Componente2.GND, VCC1.-
  N1: Componente1.VIN, R1.Pin_0, VCC1.+
  5V: Componente1.5V, Componente2.VCC
  N2: Componente1.A5, Squix1.SCL, M1.SCL, Componente2.SCL
  N3: Componente1.A4, Squix1.SCA, M1.SDA, Componente2.SDA
  N4: Componente1.A0, R1.Pin_1
  3V3: Componente1.3V3, Squix1.VCC, M1.VIN

custom parts:
  BME280: Temperature Humidity Barometric presure Sensor
  RTC DS3231: DS3231 with akku
